// Logisim project Sumador con complemento a 1.circ as structural Verilog: 2 circuits, main circuit main
module main (
  input  A3,
  input  A2,
  input  A1,
  input  A0,
  input  Cin,
  input  B0,
  input  B2,
  input  B1,
  input  B3,
  output SUM3,
  output SUM2,
  output SUM1,
  output SUM0
);

  wire adder_1_cout, not_1_out;
  wire [2:0] xor_5_out, xor_6_out;
  wire [3:0] adder_1_out, adder_2_out;

  xor xor_1 (xor_5_out[2], A2, A3);
  xor xor_2 (xor_5_out[1], A1, A3);
  xor xor_3 (xor_6_out[2], B2, B3);
  xor xor_4 (xor_6_out[1], B1, B3);
  xor xor_5 (xor_5_out[0], A0, A3);
  xor xor_6 (xor_6_out[0], B0, B3);
  Adder #(.width(4)) adder_1 (
    .a({A3, xor_5_out}), .b({B3, xor_6_out}), .out(adder_1_out), .cin(Cin), .cout(adder_1_cout));
  Adder #(.width(4)) adder_2 (.a(adder_1_out), .b(4'b0000), .out(adder_2_out), .cin(adder_1_cout));  // open: cout
  and and_1 (SUM3, not_1_out, SUM2, SUM1, SUM0);
  not not_1 (not_1_out, adder_2_out[3]);
  xor xor_7 (SUM1, adder_2_out[3], adder_2_out[1]);
  xor xor_8 (SUM2, adder_2_out[3], adder_2_out[2]);
  xor xor_9 (SUM0, adder_2_out[3], adder_2_out[0]);

  // Notes on the sheet:
  //   Operando A
  //   Operando B
endmodule

module asd (
  input  [3:0] A,
  input  Cin,
  input  [3:0] B,
  input  SumaResta,
  output [3:0] SUM
);

  wire xor_1_out;

  xor xor_1 (xor_1_out, B[3], SumaResta);
  main main_1 (
    .A3(A[3]), .A2(A[2]), .A1(A[1]), .A0(A[0]), .Cin(Cin), .B0(B[0]), .B2(B[1]), .B1(B[2]), .B3(xor_1_out),
    .SUM3(SUM[3]), .SUM2(SUM[2]), .SUM1(SUM[1]), .SUM0(SUM[0]));
endmodule
